# Fritzing sketch leddriver (saved by Fritzing 0.9.1b)
breadboards: 1

parts:
  C1 = Electrolytic Capacitor [capacitance=1mF package="100 mil [THT, electrolytic]"]
  V1 = DC Power [voltage=12V]
  IC2 = Voltage Regulator [part_number=7809 package=to-220-alt]
  L1 = Inductor [inductance=10µ package="400 mil [THT]"]
  IC1 = IC, DIP package, 8 pins [chip_label=3843]
  C2 = Electrolytic Capacitor [capacitance=25µF package="100 mil [THT, electrolytic]"]
  D1 = Schottky Diode [part_number=stps2045 package="300 mil [THT]"]
  D2 = Schottky Diode [part_number=stps2045 package="300 mil [THT]"]
  C3 = Electrolytic Capacitor [capacitance=0.1mF voltage=50V package="100 mil [THT, electrolytic]"]
  R1 = Resistor [tolerance=±5% resistance=9k package=THT]
  R2 = Resistor [tolerance=±5% resistance=15k package=THT]
  C4 = Ceramic Capacitor [capacitance=100nF package="100 mil [THT, multilayer]"]
  Q1 = NPN-Transistor [package="TO92 [THT]"]
  R3 = Resistor [tolerance=±5% resistance=10k package=THT]
  C5 = Ceramic Capacitor [capacitance=1nF package="100 mil [THT, multilayer]"]
  R4 = Rotary Potentiometer (Small) [maximum_resistance=10kΩ package=THT]
  R5 = Resistor [tolerance=±5% resistance=3k package=THT]
  R6 = Resistor [tolerance=±5% resistance=1k package=THT]
  R7 = Resistor [tolerance=±5% resistance=10k package=THT]
  D3 = Rectifier Diode [part_number=1N4007 package="300 mil [THT]"]
  R8 = Rotary Potentiometer (Small) [maximum_resistance=5kΩ package=THT]
  R9 = Resistor [tolerance=±5% resistance=1k package=THT]
  R10 = Resistor [tolerance=±5% resistance=0.05 package=THT]
  Q2 = MOSFET-NCHANNEL [package=to220v]
  R11 = Resistor [tolerance=±5% resistance=0.3 package=THT]
  output_LED = LED - 5mm [color="White (6500K)" package="5 mm [THT]"]
  R12 = Resistor [tolerance=±5% resistance=30k package=THT]

nets:
  GND: C1.-, V1.V-, IC2.GND, IC1.pin5, C2.-, C3.-, C4.1, C5.0, R6.Pin_0, R10.Pin_1, R11.Pin_1, R12.Pin_1
  N1: C1.+, V1.V+, IC2.IN, L1.pin_0, output_LED.anode
  N2: IC2.OUT, IC1.pin7
  N3: L1.pin_1, D1.anode, D2.anode, Q2.D
  N4: IC1.pin1, R7.Pin_0
  N5: IC1.pin2, D3.cathode, R8.wiper
  N6: IC1.pin3, R1.Pin_0, R3.Pin_0
  N7: IC1.pin4, R2.Pin_0, Q1.B, C5.1
  N8: IC1.pin6, Q2.G, R12.Pin_0
  N9: IC1.pin8, R1.Pin_1, R2.Pin_1, C4.0, Q1.C, R8.leg2
  N10: D1.cathode, D2.cathode, C3.+, R4.leg1, R4.wiper
  N11: Q1.E, R3.Pin_1
  N12: R4.leg2, R5.Pin_1
  N13: R5.Pin_0, R6.Pin_1, R7.Pin_1, D3.anode
  N14: R8.leg1, R11.Pin_0, output_LED.cathode
  N15: R9.Pin_1, R10.Pin_0, Q2.S
